# Fritzing sketch circuit_Refregator (saved by Fritzing 0.9.10b)
breadboards: 1

parts:
  U1 = ESP32-38PinWide [part_number=ESP32-38PinWide]
  Display1 = LCD screen 16x2 IIC [part_number=101290]
  Part1 = RFID-RC522-v2
  LED1 = LED - 5mm [color="Red (633nm)" current=0.030 package="5 mm [THT]"]
  LED2 = LED - 5mm [color="Green (570nm)" current=30mA package="5 mm [THT]"]
  J1 = Piezo Speaker
  KF-1 = KF-301 Relay [package=THT]
  F1 = Fan - Ventilador [package=THT]
  F2 = Fan - Ventilador [package=THT]
  S1 = H-Bridge with L298N
  RHT1 = Humidity and Temperature Sensor RHT03
  VCC1 = 4 x AAA Battery Mount

nets:
  N1: U1.3.3, Part1.3.3V
  N2: U1.GPIO34, LED1.anode
  N3: U1.GPIO35, J1.pin2
  N4: U1.GPIO32, S1.IN3
  N5: U1.GPIO33, S1.IN2
  N6: U1.GPIO25, S1.IN1
  N7: U1.GPIO26, S1.ENB
  N8: U1.GPIO27, S1.ENA
  N9: U1.GPIO14, S1.IN4
  N10: U1.GPIO12, KF-1.signal
  N11: U1.GPIO13, RHT1.GND_1
  VIN: U1.VIN, Display1.VCC
  N12: U1.GPIO4, Part1.RST
  N13: U1.GPIO16, LED2.anode
  N14: U1.GPIO5, Part1.SDA
  N15: U1.GPIO18, Part1.SCK
  N16: U1.GPIO19, Part1.MISO
  N17: U1.GPIO21, Display1.SDA
  N18: U1.GPIO22, Display1.SCL
  N19: U1.GPIO23, Part1.MOSI
  GND: U1.GND, Part1.GND
  N20: Display1.GND, LED2.cathode, KF-1.ground
  N21: F1.5V, S1.M1-02
  N22: F1.GND, S1.M1-01
  N23: F2.GND, S1.M2-01
  N24: S1.12V, VCC1.+
  N25: S1.GND, VCC1.-

custom parts:
  ESP32-38PinWide: Generic 38-Pin ESP32 with wide format (only access to one side of pins on a breadboard) based on Stephen Lilley's HiLetgo ESP-WROOM-32 ESP32 ESP-32S Development Board.
  LCD screen 16x2 IIC: LCD screen with HD44780 controller enables showing text, symbols, value or anything else that comes from Croduino/Arduino. It is capable of showing 16 symbols in two lines and therefore can be used in many projects that need to send clearly visible and legible output information.. • Color of symbols: White • Backlight: Blue • Dimensions: 80 x 36 x 12 mm • Screen dimensions: 64.5 x 16 mm •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
  RFID-RC522-v2: A simple China made RFID-RC522 Reader; do check the pin labels, as this is a MFRC522 based clone.
  KF-301 Relay: KF-301
  Fan - Ventilador: Ventilador de 2 pines, se encuentra comunmente en computadoras de escritorio
  H-Bridge with L298N: h-bridge
